// Logisim project assn5.circ as structural Verilog: 3 circuits, main circuit main
module main (
);

  wire _0_out, _1_out, _2_out, _3_out, _4_out, _5_out, _6_out, _7_out, _8_out, _9_out, CLEAR_out, d_ff_1_q,
       d_ff_2_q, d_ff_3_qn, d_ff_4_q, d_ff_5_qn, n74147_1_a, n74147_1_b, n74147_1_c, n74147_1_d, nor_1_out,
       not_1_out, not_2_out, not_3_out, not_4_out, not_5_out, not_6_out, not_7_out, not_8_out, not_9_out;
  wire [3:0] not_10_out, register_1_q, register_2_q, register_3_q;
  wire [6:0] n7446_1_a_2, n7446_2_a_2, n7446_3_a_2;

  Button _0 (.out(_0_out));
  Button _3 (.out(_3_out));
  Button _2 (.out(_2_out));
  Button _5 (.out(_5_out));
  Button _6 (.out(_6_out));
  Button _8 (.out(_8_out));
  Button _9 (.out(_9_out));
  Button _1 (.out(_1_out));
  Button _4 (.out(_4_out));
  Button _7 (.out(_7_out));
  not not_1 (not_1_out, _1_out);
  not not_2 (not_2_out, _2_out);
  not not_3 (not_3_out, _3_out);
  not not_4 (not_4_out, _4_out);
  not not_5 (not_5_out, _5_out);
  not not_6 (not_6_out, _6_out);
  not not_7 (not_7_out, _7_out);
  not not_8 (not_8_out, _8_out);
  not not_9 (not_9_out, _9_out);
  Button CLEAR (.out(CLEAR_out));
  not not_10 (not_10_out[0], n74147_1_a);
  not not_11 (not_10_out[1], n74147_1_b);
  not not_12 (not_10_out[2], n74147_1_c);
  _74147 u_74147_1 (
    ._1(not_1_out), ._2(not_2_out), ._3(not_3_out), ._4(not_4_out), ._5(not_5_out), ._6(not_6_out),
    ._7(not_7_out), ._8(not_8_out), ._9(not_9_out), .D(n74147_1_d), .C(n74147_1_c), .B(n74147_1_b),
    .A(n74147_1_a));
  not not_13 (not_10_out[3], n74147_1_d);
  nor nor_1 (nor_1_out, not_10_out[3], not_10_out[2], not_10_out[1], not_10_out[0], _0_out);
  D_Flip_Flop #(.trigger("falling")) d_ff_1 (
    .clk(nor_1_out), .D(d_ff_4_q), .Q(d_ff_1_q), .preset(CLEAR_out), .en(d_ff_5_qn), .reset(1'b0));  // open: Qn
  D_Flip_Flop #(.trigger("falling")) d_ff_2 (
    .clk(nor_1_out), .D(d_ff_1_q), .Q(d_ff_2_q), .preset(1'b0), .en(d_ff_5_qn), .reset(CLEAR_out));  // open: Qn
  D_Flip_Flop d_ff_3 (.clk(d_ff_1_q), .Qn(d_ff_3_qn), .reset(CLEAR_out));  // open: D, Q, preset, en
  D_Flip_Flop #(.trigger("falling")) d_ff_4 (
    .clk(nor_1_out), .D(d_ff_2_q), .Q(d_ff_4_q), .preset(1'b0), .en(d_ff_5_qn), .reset(CLEAR_out));  // open: Qn
  D_Flip_Flop d_ff_5 (.clk(d_ff_1_q), .D(d_ff_3_qn), .Qn(d_ff_5_qn), .reset(CLEAR_out));  // open: Q, preset, en
  Register #(.width(4), .trigger("falling")) register_1 (
    .D(not_10_out), .Q(register_1_q), .clk(d_ff_1_q), .clr(CLEAR_out));  // open: en
  Register #(.width(4), .trigger("falling")) register_2 (
    .D(not_10_out), .Q(register_2_q), .clk(d_ff_2_q), .clr(CLEAR_out));  // open: en
  Register #(.width(4), .trigger("falling")) register_3 (
    .D(not_10_out), .Q(register_3_q), .clk(d_ff_4_q), .clr(CLEAR_out));  // open: en
  _7_Segment_Display u_7_segment_display_1 (
    .g(n7446_2_a_2[6]), .f(n7446_2_a_2[5]), .a(n7446_2_a_2[0]), .b(n7446_2_a_2[1]), .e(n7446_2_a_2[4]),
    .d(n7446_2_a_2[3]), .c(n7446_2_a_2[2]));  // open: dp
  _7_Segment_Display u_7_segment_display_2 (
    .g(n7446_1_a_2[6]), .f(n7446_1_a_2[5]), .a(n7446_1_a_2[0]), .b(n7446_1_a_2[1]), .e(n7446_1_a_2[4]),
    .d(n7446_1_a_2[3]), .c(n7446_1_a_2[2]));  // open: dp
  _7446 u_7446_1 (
    .BI(1'b1), .LT(1'b1), .RBI(1'b1), .D(register_1_q[3]), .C(register_1_q[2]), .B(register_1_q[1]),
    .A(register_1_q[0]), .a_2(n7446_1_a_2[0]), .b_2(n7446_1_a_2[1]), .c_2(n7446_1_a_2[2]),
    .d_2(n7446_1_a_2[3]), .e(n7446_1_a_2[4]), .f(n7446_1_a_2[5]), .g(n7446_1_a_2[6]));
  _7446 u_7446_2 (
    .BI(1'b1), .LT(1'b1), .RBI(1'b1), .D(register_2_q[3]), .C(register_2_q[2]), .B(register_2_q[1]),
    .A(register_2_q[0]), .a_2(n7446_2_a_2[0]), .b_2(n7446_2_a_2[1]), .c_2(n7446_2_a_2[2]),
    .d_2(n7446_2_a_2[3]), .e(n7446_2_a_2[4]), .f(n7446_2_a_2[5]), .g(n7446_2_a_2[6]));
  _7446 u_7446_3 (
    .BI(1'b1), .LT(1'b1), .RBI(1'b1), .D(register_3_q[3]), .C(register_3_q[2]), .B(register_3_q[1]),
    .A(register_3_q[0]), .a_2(n7446_3_a_2[0]), .b_2(n7446_3_a_2[1]), .c_2(n7446_3_a_2[2]),
    .d_2(n7446_3_a_2[3]), .e(n7446_3_a_2[4]), .f(n7446_3_a_2[5]), .g(n7446_3_a_2[6]));
  _7_Segment_Display u_7_segment_display_3 (
    .g(n7446_3_a_2[6]), .f(n7446_3_a_2[5]), .a(n7446_3_a_2[0]), .b(n7446_3_a_2[1]), .e(n7446_3_a_2[4]),
    .d(n7446_3_a_2[3]), .c(n7446_3_a_2[2]));  // open: dp

  // Notes on the sheet:
  //   * The clear button must be pressed before the circuit will operate correctly
endmodule

module _7446 (
  input  BI,
  input  LT,
  input  RBI,
  input  D,
  input  C,
  input  B,
  input  A,
  output a_2,
  output b_2,
  output c_2,
  output d_2,
  output e,
  output f,
  output g
);

  wire and_1_out, and_2_out, and_3_out, and_4_out, and_5_out, and_6_out, and_7_out, and_8_out, and_9_out,
       and_10_out, and_11_out, and_12_out, and_13_out, and_14_out, and_15_out, and_16_out, and_17_out,
       and_18_out, and_19_out, and_20_out, and_21_out, and_22_out, and_23_out, and_24_out, and_25_out,
       and_26_out, and_27_out, and_28_out, and_29_out, and_30_out, and_31_out, and_32_out, and_33_out,
       and_34_out, and_35_out, and_36_out, and_37_out, and_38_out, not_1_out, not_2_out, not_3_out,
       not_4_out, not_5_out, not_6_out, not_7_out, not_8_out, not_9_out, not_10_out, not_11_out, not_12_out,
       not_13_out, not_14_out, not_15_out, not_16_out, not_17_out, not_18_out, not_19_out, not_20_out,
       not_21_out, not_22_out, not_23_out, not_24_out, not_25_out, not_26_out, not_27_out, not_28_out,
       not_29_out, not_30_out, not_31_out, not_32_out, not_33_out, not_34_out, not_35_out, not_36_out,
       not_37_out, not_38_out, not_39_out, not_40_out, not_41_out, not_42_out, not_43_out, not_44_out,
       not_45_out, not_46_out, not_47_out, not_48_out, not_49_out, not_50_out, not_51_out, not_52_out,
       not_53_out, not_54_out;

  Pull_Resistor #(.pull(1)) pull_resistor_1 (.node(BI));
  Pull_Resistor #(.pull(1)) pull_resistor_2 (.node(RBI));
  Pull_Resistor #(.pull(1)) pull_resistor_3 (.node(LT));
  not not_1 (not_1_out, LT);
  not not_2 (not_2_out, D);
  not not_3 (not_3_out, C);
  not not_4 (not_4_out, D);
  not not_5 (not_5_out, C);
  not not_6 (not_6_out, B);
  not not_7 (not_7_out, B);
  not not_8 (not_8_out, D);
  not not_9 (not_9_out, C);
  not not_10 (not_10_out, A);
  not not_11 (not_11_out, LT);
  not not_12 (not_12_out, D);
  not not_13 (not_13_out, C);
  not not_14 (not_14_out, D);
  not not_15 (not_15_out, C);
  not not_16 (not_16_out, D);
  not not_17 (not_17_out, B);
  not not_18 (not_18_out, A);
  not not_19 (not_19_out, C);
  not not_20 (not_20_out, B);
  not not_21 (not_21_out, D);
  not not_22 (not_22_out, C);
  not not_23 (not_23_out, LT);
  not not_24 (not_24_out, C);
  not not_25 (not_25_out, D);
  not not_26 (not_26_out, C);
  not not_27 (not_27_out, B);
  not not_28 (not_28_out, D);
  not not_29 (not_29_out, B);
  not not_30 (not_30_out, LT);
  not not_31 (not_31_out, C);
  not not_32 (not_32_out, A);
  not not_33 (not_33_out, B);
  not not_34 (not_34_out, C);
  not not_35 (not_35_out, A);
  not not_36 (not_36_out, C);
  not not_37 (not_37_out, A);
  not not_38 (not_38_out, LT);
  not not_39 (not_39_out, A);
  not not_40 (not_40_out, C);
  not not_41 (not_41_out, A);
  not not_42 (not_42_out, C);
  not not_43 (not_43_out, A);
  not not_44 (not_44_out, LT);
  not not_45 (not_45_out, B);
  not not_46 (not_46_out, A);
  not not_47 (not_47_out, B);
  not not_48 (not_48_out, B);
  not not_49 (not_49_out, A);
  not not_50 (not_50_out, LT);
  not not_51 (not_51_out, C);
  not not_52 (not_52_out, B);
  not not_53 (not_53_out, A);
  not not_54 (not_54_out, C);
  and and_1 (and_1_out, BI, not_1_out);
  and and_2 (and_2_out, BI, not_2_out, not_3_out, B);
  and and_3 (and_3_out, BI, not_4_out, C, A);
  and and_4 (and_4_out, BI, D, not_5_out, not_6_out);
  and and_5 (and_5_out, BI, D, not_7_out, A);
  and and_6 (and_6_out, BI, RBI, not_8_out, not_9_out, not_10_out);
  and and_7 (and_7_out, BI, not_11_out);
  and and_8 (and_8_out, BI, not_12_out, not_13_out, A);
  and and_9 (and_9_out, BI, not_14_out, not_15_out, B);
  and and_10 (and_10_out, BI, not_16_out, B, A);
  and and_11 (and_11_out, BI, C, not_17_out, not_18_out);
  and and_12 (and_12_out, BI, D, not_19_out, not_20_out);
  and and_13 (and_13_out, BI, RBI, not_21_out, not_22_out);
  and and_14 (and_14_out, BI, not_23_out);
  and and_15 (and_15_out, BI, not_24_out, A);
  and and_16 (and_16_out, BI, not_25_out, C);
  and and_17 (and_17_out, BI, D, not_26_out, not_27_out);
  and and_18 (and_18_out, BI, RBI, not_28_out, not_29_out);
  and and_19 (and_19_out, BI, not_30_out);
  and and_20 (and_20_out, BI, not_31_out, B);
  and and_21 (and_21_out, BI, B, not_32_out);
  and and_22 (and_22_out, BI, C, not_33_out, A);
  and and_23 (and_23_out, BI, D, not_34_out, not_35_out);
  and and_24 (and_24_out, BI, RBI, not_36_out, not_37_out);
  and and_25 (and_25_out, BI, not_38_out);
  and and_26 (and_26_out, BI, B, not_39_out);
  and and_27 (and_27_out, BI, D, not_40_out, not_41_out);
  and and_28 (and_28_out, BI, RBI, not_42_out, not_43_out);
  and and_29 (and_29_out, BI, not_44_out);
  and and_30 (and_30_out, BI, C, not_45_out);
  and and_31 (and_31_out, BI, C, not_46_out);
  and and_32 (and_32_out, BI, D, not_47_out);
  and and_33 (and_33_out, BI, RBI, not_48_out, not_49_out);
  and and_34 (and_34_out, BI, not_50_out);
  and and_35 (and_35_out, BI, not_51_out, B);
  and and_36 (and_36_out, BI, C, not_52_out);
  and and_37 (and_37_out, BI, C, not_53_out);
  and and_38 (and_38_out, BI, D, not_54_out);
  or or_1 (a_2, and_1_out, and_2_out, and_3_out, and_4_out, and_5_out, and_6_out);
  or or_2 (b_2, and_7_out, and_8_out, and_9_out, and_10_out, and_11_out, and_12_out, and_13_out);
  or or_3 (c_2, and_14_out, and_15_out, and_16_out, and_17_out, and_18_out);
  or or_4 (d_2, and_19_out, and_20_out, and_21_out, and_22_out, and_23_out, and_24_out);
  or or_5 (e, and_25_out, and_26_out, and_27_out, and_28_out);
  or or_6 (f, and_29_out, and_30_out, and_31_out, and_32_out, and_33_out);
  or or_7 (g, and_34_out, and_35_out, and_36_out, and_37_out, and_38_out);
endmodule

module _74147 (
  input  _1,
  input  _2,
  input  _3,
  input  _4,
  input  _5,
  input  _6,
  input  _7,
  input  _8,
  input  _9,
  output D,
  output C,
  output B,
  output A
);

  wire and_2_out, and_3_out, and_4_out, and_5_out, and_6_out, and_7_out, and_8_out, and_9_out, and_10_out,
       not_1_out, not_2_out, not_3_out, not_4_out, not_5_out, not_6_out, not_7_out, not_8_out, not_9_out,
       not_10_out;

  and and_1 (D, _9, _8);
  not not_1 (not_1_out, _8);
  not not_2 (not_2_out, _9);
  and and_2 (and_2_out, _4, _5, _6, _7);
  not not_3 (not_3_out, _4);
  not not_4 (not_4_out, _5);
  not not_5 (not_5_out, _8);
  not not_6 (not_6_out, _6);
  not not_7 (not_7_out, _4);
  not not_8 (not_8_out, _2);
  or or_1 (C, not_1_out, not_2_out, and_2_out);
  not not_9 (not_9_out, _8);
  not not_10 (not_10_out, _9);
  and and_3 (and_3_out, not_3_out, _6, _7);
  and and_4 (and_4_out, not_4_out, _6, _7);
  and and_5 (and_5_out, _2, _3, _6, _7);
  and and_6 (and_6_out, not_5_out, _9);
  and and_7 (and_7_out, not_6_out, _7, _9);
  and and_8 (and_8_out, not_7_out, _5, _7, _9);
  and and_9 (and_9_out, not_8_out, _3, _5, _7, _9);
  and and_10 (and_10_out, _1, _3, _5, _7, _9);
  or or_2 (B, not_9_out, not_10_out, and_3_out, and_4_out, and_5_out);
  or or_3 (A, and_6_out, and_7_out, and_8_out, and_9_out, and_10_out);
endmodule
